# Fritzing sketch board (saved by Fritzing 0.9.2b)
perfboards: 1

parts:
  U1 = LM 358 Dual Op-Amp [package="DIP8 [THT]"]
  R1 = Resistor [tolerance=±5% resistance=220 package=THT]
  R2 = Resistor [tolerance=±5% resistance=220 package=THT]
  R3 = Resistor [tolerance=±5% resistance=220 package=THT]
  R4 = Resistor [tolerance=±5% resistance=220 package=THT]
  Part1 = Arduino Nano (Rev3.0)  # not connected
  C2 = Ceramic Capacitor [capacitance=100nF package="100 mil [THT, multilayer]"]
  R5 = Resistor [tolerance=±5% resistance=220 package=THT]  # not connected
  C3 = Ceramic Capacitor [capacitance=100nF package="100 mil [THT, multilayer]"]  # not connected
  U2 = LM 358 Dual Op-Amp [package="DIP8 [THT]"]
  R7 = Resistor [tolerance=±5% resistance=220 package=THT]
  R8 = Resistor [tolerance=±5% resistance=220 package=THT]
  C4 = Ceramic Capacitor [capacitance=100nF package="100 mil [THT, multilayer]"]  # not connected
  R9 = Resistor [tolerance=±5% resistance=220 package=THT]  # not connected

nets:
  N1: U1.connector0, R3.Pin_1
  N2: U1.connector1, R3.Pin_0
  N3: U1.connector2, U1.connector4
  N4: R1.Pin_1, R2.Pin_0, U2.connector4
  N5: R4.Pin_1, C2.0
  N6: U2.connector5, R7.Pin_1
  N7: U2.connector6, R7.Pin_0, R8.Pin_1
